// Logisim project control-logic.circ as structural Verilog: 1 circuit, main circuit control_logic
module control_logic (
  input  [31:0] Instruction,
  input  BrEq,
  input  BrLt,
  output PCSel,
  output RegWEn,
  output [2:0] ImmSel,
  output BrUn,
  output ASel,
  output BSel,
  output [3:0] ALUSel,
  output MemWEn,
  output [1:0] WBSel
);

  wire and_1_out, and_2_out, and_3_out, and_4_out, and_5_out, and_6_out, and_7_out, and_16_out, and_17_out,
       and_21_out, comparator_1_eq, comparator_2_eq, comparator_3_eq, comparator_4_eq, comparator_5_eq,
       comparator_6_eq, comparator_8_eq, comparator_9_eq, comparator_10_eq, comparator_11_eq,
       comparator_12_eq, comparator_13_eq, comparator_14_eq, comparator_15_eq, comparator_16_eq,
       comparator_17_eq, comparator_18_eq, comparator_19_eq, comparator_20_eq, comparator_22_eq,
       comparator_23_eq, comparator_24_eq, comparator_25_eq, comparator_26_eq, comparator_28_eq,
       comparator_29_eq, comparator_30_eq, comparator_32_eq, comparator_33_eq, comparator_34_eq,
       comparator_35_eq, comparator_36_eq, comparator_42_eq, comparator_43_eq, comparator_44_eq,
       comparator_45_eq, comparator_46_eq, comparator_47_eq, is_add, is_addi, is_and, is_andi, is_auipc,
       is_B_type, is_beq, is_bge, is_bgeu, is_blt, is_bltu, is_bne, is_I_type, is_jal, is_jalr, is_lb, is_lh,
       is_Load, is_lui, is_lw, is_mul, is_mulh, is_mulhu, is_or, is_ori, is_R_type, is_S_type, is_sb, is_sh,
       is_sll, is_slli, is_slt, is_slti, is_sra, is_srai, is_srl, is_srli, is_sub, is_sw, is_xor, is_xori,
       not_1_out, not_2_out, or_1_out, or_2_out, or_3_out;
  wire [5:0] ROMInput;
  wire [15:14] rom_1_data;

  ROM #(.addrWidth(6), .dataWidth(16)) rom_1 (
    .addr(ROMInput), .data({rom_1_data, WBSel, MemWEn, ALUSel, BSel, ASel, BrUn, ImmSel, RegWEn}));
  Priority_Encoder #(.select_enc(6)) priority_encoder_1 (
    .in0(is_add), .in1(is_mul), .in2(is_sub), .in3(is_sll), .in4(is_mulh), .in5(is_mulhu), .in6(is_slt),
    .in7(is_xor), .in8(is_srl), .in9(is_sra), .in10(is_or), .in11(is_and), .in12(is_lb), .in13(is_lh),
    .in14(is_lw), .in15(is_addi), .in16(is_slli), .in17(is_slti), .in18(is_xori), .in19(is_srli),
    .in20(is_srai), .in21(is_ori), .in22(is_andi), .in23(is_sb), .in24(is_sh), .in25(is_sw), .in26(is_beq),
    .in27(is_bne), .in28(is_blt), .in29(is_bge), .in30(is_bltu), .in31(is_bgeu), .in32(is_auipc),
    .in33(is_lui), .in34(is_jal), .in35(is_jalr), .out(ROMInput));  // open: in36, in37, in38, in39, in40, in41, in42, in43, in44, in45, in46, in47, in48, in49, in50, in51, in52, in53, in54, in55, in56, in57, in58, in59, in60, in61, in62, in63, gs, en_out, en_in
  or or_1 (or_1_out, is_blt, is_bltu);
  not not_1 (not_1_out, BrLt);
  or or_2 (or_2_out, is_bge, is_bgeu);
  and and_1 (and_1_out, is_beq, BrEq);
  not not_2 (not_2_out, BrEq);
  and and_2 (and_2_out, not_2_out, is_bne);
  and and_3 (and_3_out, or_1_out, BrLt);
  and and_4 (and_4_out, not_1_out, or_2_out);
  Comparator #(.width(3)) comparator_1 (.a(3'b001), .b(Instruction[14:12]), .eq(comparator_1_eq));  // open: gt, lt
  Comparator #(.width(3)) comparator_2 (.a(3'b101), .b(Instruction[14:12]), .eq(comparator_2_eq));  // open: gt, lt
  Comparator #(.width(3)) comparator_3 (.a(3'b101), .b(Instruction[14:12]), .eq(comparator_3_eq));  // open: gt, lt
  Comparator #(.width(7)) comparator_4 (.a({7{1'b0}}), .b(Instruction[31:25]), .eq(comparator_4_eq));  // open: gt, lt
  and and_5 (and_5_out, is_I_type, comparator_1_eq);
  Comparator #(.width(7)) comparator_5 (.a({7{1'b0}}), .b(Instruction[31:25]), .eq(comparator_5_eq));  // open: gt, lt
  and and_6 (and_6_out, is_I_type, comparator_2_eq);
  Comparator #(.width(7)) comparator_6 (.a(7'b0100000), .b(Instruction[31:25]), .eq(comparator_6_eq));  // open: gt, lt
  and and_7 (and_7_out, is_I_type, comparator_3_eq);
  or or_3 (or_3_out, and_1_out, and_2_out, and_3_out, and_4_out);
  Comparator #(.width(7)) comparator_7 (.a(7'b0010011), .b(Instruction[6:0]), .eq(is_I_type));  // open: gt, lt
  Comparator #(.width(3)) comparator_8 (.a(3'b000), .b(Instruction[14:12]), .eq(comparator_8_eq));  // open: gt, lt
  and and_8 (is_slli, comparator_4_eq, and_5_out);
  Comparator #(.width(3)) comparator_9 (.a(3'b010), .b(Instruction[14:12]), .eq(comparator_9_eq));  // open: gt, lt
  Comparator #(.width(3)) comparator_10 (.a(3'b100), .b(Instruction[14:12]), .eq(comparator_10_eq));  // open: gt, lt
  and and_9 (is_srli, comparator_5_eq, and_6_out);
  and and_10 (is_srai, comparator_6_eq, and_7_out);
  Comparator #(.width(3)) comparator_11 (.a(3'b110), .b(Instruction[14:12]), .eq(comparator_11_eq));  // open: gt, lt
  Comparator #(.width(3)) comparator_12 (.a(3'b111), .b(Instruction[14:12]), .eq(comparator_12_eq));  // open: gt, lt
  or or_4 (PCSel, is_jal, is_jalr, or_3_out);
  and and_11 (is_addi, is_I_type, comparator_8_eq);
  and and_12 (is_slti, is_I_type, comparator_9_eq);
  and and_13 (is_xori, is_I_type, comparator_10_eq);
  and and_14 (is_ori, is_I_type, comparator_11_eq);
  and and_15 (is_andi, is_I_type, comparator_12_eq);
  Comparator #(.width(3)) comparator_13 (.a(3'b000), .b(Instruction[14:12]), .eq(comparator_13_eq));  // open: gt, lt
  Comparator #(.width(3)) comparator_14 (.a(3'b001), .b(Instruction[14:12]), .eq(comparator_14_eq));  // open: gt, lt
  Comparator #(.width(3)) comparator_15 (.a(3'b010), .b(Instruction[14:12]), .eq(comparator_15_eq));  // open: gt, lt
  Comparator #(.width(3)) comparator_16 (.a(3'b011), .b(Instruction[14:12]), .eq(comparator_16_eq));  // open: gt, lt
  Comparator #(.width(3)) comparator_17 (.a(3'b100), .b(Instruction[14:12]), .eq(comparator_17_eq));  // open: gt, lt
  Comparator #(.width(3)) comparator_18 (.a(3'b101), .b(Instruction[14:12]), .eq(comparator_18_eq));  // open: gt, lt
  Comparator #(.width(3)) comparator_19 (.a(3'b110), .b(Instruction[14:12]), .eq(comparator_19_eq));  // open: gt, lt
  Comparator #(.width(3)) comparator_20 (.a(3'b111), .b(Instruction[14:12]), .eq(comparator_20_eq));  // open: gt, lt
  Comparator #(.width(7)) comparator_21 (.a(7'b0110011), .b(Instruction[6:0]), .eq(is_R_type));  // open: gt, lt
  Comparator #(.width(7)) comparator_22 (.a({7{1'b0}}), .b(Instruction[31:25]), .eq(comparator_22_eq));  // open: gt, lt
  and and_16 (and_16_out, is_R_type, comparator_13_eq);
  Comparator #(.width(7)) comparator_23 (
    .a(7'b0000001), .b(Instruction[31:25]), .eq(comparator_23_eq));  // open: gt, lt
  Comparator #(.width(7)) comparator_24 (
    .a(7'b0100000), .b(Instruction[31:25]), .eq(comparator_24_eq));  // open: gt, lt
  Comparator #(.width(7)) comparator_25 (.a({7{1'b0}}), .b(Instruction[31:25]), .eq(comparator_25_eq));  // open: gt, lt
  and and_17 (and_17_out, is_R_type, comparator_14_eq);
  and and_18 (is_slt, is_R_type, comparator_15_eq);
  and and_19 (is_mulhu, is_R_type, comparator_16_eq);
  and and_20 (is_xor, is_R_type, comparator_17_eq);
  Comparator #(.width(7)) comparator_26 (.a({7{1'b0}}), .b(Instruction[31:25]), .eq(comparator_26_eq));  // open: gt, lt
  and and_21 (and_21_out, is_R_type, comparator_18_eq);
  and and_22 (is_or, is_R_type, comparator_19_eq);
  and and_23 (is_and, is_R_type, comparator_20_eq);
  Comparator #(.width(7)) comparator_27 (.a(7'b0000011), .b(Instruction[6:0]), .eq(is_Load));  // open: gt, lt
  Comparator #(.width(3)) comparator_28 (.a(3'b000), .b(Instruction[14:12]), .eq(comparator_28_eq));  // open: gt, lt
  Comparator #(.width(3)) comparator_29 (.a(3'b001), .b(Instruction[14:12]), .eq(comparator_29_eq));  // open: gt, lt
  Comparator #(.width(3)) comparator_30 (.a(3'b010), .b(Instruction[14:12]), .eq(comparator_30_eq));  // open: gt, lt
  Comparator #(.width(7)) comparator_31 (.a(7'b0100011), .b(Instruction[6:0]), .eq(is_S_type));  // open: gt, lt
  Comparator #(.width(3)) comparator_32 (.a(3'b000), .b(Instruction[14:12]), .eq(comparator_32_eq));  // open: gt, lt
  Comparator #(.width(3)) comparator_33 (.a(3'b001), .b(Instruction[14:12]), .eq(comparator_33_eq));  // open: gt, lt
  Comparator #(.width(3)) comparator_34 (.a(3'b010), .b(Instruction[14:12]), .eq(comparator_34_eq));  // open: gt, lt
  and and_24 (is_add, comparator_22_eq, and_16_out);
  and and_25 (is_mul, and_16_out, comparator_23_eq);
  and and_26 (is_sub, and_16_out, comparator_24_eq);
  Comparator #(.width(7)) comparator_35 (
    .a(7'b0000001), .b(Instruction[31:25]), .eq(comparator_35_eq));  // open: gt, lt
  Comparator #(.width(7)) comparator_36 (
    .a(7'b0100000), .b(Instruction[31:25]), .eq(comparator_36_eq));  // open: gt, lt
  and and_27 (is_lb, is_Load, comparator_28_eq);
  and and_28 (is_lh, is_Load, comparator_29_eq);
  and and_29 (is_lw, is_Load, comparator_30_eq);
  and and_30 (is_sb, is_S_type, comparator_32_eq);
  and and_31 (is_sh, is_S_type, comparator_33_eq);
  and and_32 (is_sw, is_S_type, comparator_34_eq);
  and and_33 (is_sll, comparator_25_eq, and_17_out);
  and and_34 (is_mulh, and_17_out, comparator_35_eq);
  and and_35 (is_srl, comparator_26_eq, and_21_out);
  and and_36 (is_sra, and_21_out, comparator_36_eq);
  Comparator #(.width(7)) comparator_37 (.a(7'b1101111), .b(Instruction[6:0]), .eq(is_jal));  // open: gt, lt
  Comparator #(.width(7)) comparator_38 (.a(7'b1100111), .b(Instruction[6:0]), .eq(is_jalr));  // open: gt, lt
  Comparator #(.width(7)) comparator_39 (.a(7'b0010111), .b(Instruction[6:0]), .eq(is_auipc));  // open: gt, lt
  Comparator #(.width(7)) comparator_40 (.a(7'b0110111), .b(Instruction[6:0]), .eq(is_lui));  // open: gt, lt
  Comparator #(.width(7)) comparator_41 (.a(7'b1100011), .b(Instruction[6:0]), .eq(is_B_type));  // open: gt, lt
  Comparator #(.width(3)) comparator_42 (.a(3'b000), .b(Instruction[14:12]), .eq(comparator_42_eq));  // open: gt, lt
  Comparator #(.width(3)) comparator_43 (.a(3'b001), .b(Instruction[14:12]), .eq(comparator_43_eq));  // open: gt, lt
  Comparator #(.width(3)) comparator_44 (.a(3'b100), .b(Instruction[14:12]), .eq(comparator_44_eq));  // open: gt, lt
  Comparator #(.width(3)) comparator_45 (.a(3'b101), .b(Instruction[14:12]), .eq(comparator_45_eq));  // open: gt, lt
  Comparator #(.width(3)) comparator_46 (.a(3'b110), .b(Instruction[14:12]), .eq(comparator_46_eq));  // open: gt, lt
  Comparator #(.width(3)) comparator_47 (.a(3'b111), .b(Instruction[14:12]), .eq(comparator_47_eq));  // open: gt, lt
  and and_37 (is_beq, is_B_type, comparator_42_eq);
  and and_38 (is_bne, is_B_type, comparator_43_eq);
  and and_39 (is_blt, is_B_type, comparator_44_eq);
  and and_40 (is_bge, is_B_type, comparator_45_eq);
  and and_41 (is_bltu, is_B_type, comparator_46_eq);
  and and_42 (is_bgeu, is_B_type, comparator_47_eq);

  // Other names for the same wires on the sheet: opcode[6:0] = Instruction[6:0]; func3[2:0] = Instruction[14:12]

  // Notes on the sheet:
  //   INPUTS to your circuit
  //   contents of rom_1 (hex, n*v repeats v):
  //   1001 1401 1601 1081 1481 1581 1101 1201 1281 1681 1301 1381 41 41 41 1041 10c1 1141 1241 12c1 16c1
  //   1341 13c1 1842 1842 1842 4*1064 1074 1074 1067 17c7 2069 2041
  //   ROM FOR CONTROL LOGIC
  //   DON'T CHANGE THE LOCATIONS OF THE INPUTS AND OUTPUTS!
  //   This is only if you choose to do the ROM option
  //   CONNECT
  //   WIRE
  //   TO
  //   USE
  //   ROM
  //   OUTPUT from your circuit
  //   Reminder: If using ROM, use combinational logic for PCSel
  //   I-Type
  //   R-Type
  //   Load
  //   S-Type
  //   J-Type
  //   JALR
  //   U-Type
  //   B-Type
endmodule
