// Logisim project imm-gen.circ as structural Verilog: 1 circuit, main circuit imm_gen
module imm_gen (
  input  [31:0] Instruction,
  input  [2:0] ImmSel,
  output [31:0] Immediate
);

  wire [31:0] adder_1_out, adder_2_out, adder_3_out, adder_4_out, adder_5_out, B_imme, bit_extender_1_out,
       bit_extender_2_out, bit_extender_3_out, bit_extender_4_out, bit_extender_5_out, bit_extender_6_out,
       bit_extender_7_out, bit_extender_8_out, bit_extender_9_out, bit_extender_10_out, bit_extender_11_out,
       bit_extender_12_out, I_imme, J_imme, S_imme, shifter_1_out, shifter_2_out, shifter_4_out,
       shifter_5_out, shifter_6_out, shifter_7_out, shifter_8_out, shifter_9_out, shifter_10_out,
       shifter_11_out, U_imme;

  assign bit_extender_1_out = {{31{1'b0}}, Instruction[7]};  // Bit_Extender bit_extender_1
  assign bit_extender_2_out = {{28{1'b0}}, Instruction[11:8]};  // Bit_Extender bit_extender_2
  assign bit_extender_3_out = {{26{1'b0}}, Instruction[30:25]};  // Bit_Extender bit_extender_3
  assign bit_extender_4_out = {{31{Instruction[31]}}, Instruction[31]};  // Bit_Extender bit_extender_4
  assign bit_extender_5_out = {{27{1'b0}}, Instruction[11:7]};  // Bit_Extender bit_extender_5
  assign bit_extender_6_out = {{26{1'b0}}, Instruction[30:25]};  // Bit_Extender bit_extender_6
  assign bit_extender_7_out = {{31{Instruction[31]}}, Instruction[31]};  // Bit_Extender bit_extender_7
  assign bit_extender_8_out = {{12{1'b0}}, Instruction[31:12]};  // Bit_Extender bit_extender_8
  assign bit_extender_9_out = {{31{1'b0}}, Instruction[20]};  // Bit_Extender bit_extender_9
  assign bit_extender_10_out = {{24{1'b0}}, Instruction[19:12]};  // Bit_Extender bit_extender_10
  assign bit_extender_11_out = {{22{1'b0}}, Instruction[30:21]};  // Bit_Extender bit_extender_11
  assign bit_extender_12_out = {{31{Instruction[31]}}, Instruction[31]};  // Bit_Extender bit_extender_12
  Shifter #(.width(32)) shifter_1 (.in(bit_extender_6_out), .\dist (5'b00101), .out(shifter_1_out));
  Shifter #(.width(32)) shifter_2 (.in(bit_extender_7_out), .\dist (5'b01011), .out(shifter_2_out));
  Shifter #(.width(32)) shifter_3 (.in(bit_extender_8_out), .\dist (5'b01100), .out(U_imme));
  Shifter #(.width(32)) shifter_4 (.in(bit_extender_9_out), .\dist (5'b01011), .out(shifter_4_out));
  Shifter #(.width(32)) shifter_5 (.in(bit_extender_10_out), .\dist (5'b01100), .out(shifter_5_out));
  Shifter #(.width(32)) shifter_6 (.in(bit_extender_11_out), .\dist (5'b00001), .out(shifter_6_out));
  Shifter #(.width(32)) shifter_7 (.in(bit_extender_12_out), .\dist (5'b10100), .out(shifter_7_out));
  Multiplexer #(.select(3), .width(32)) multiplexer_1 (
    .in0(I_imme), .in1(S_imme), .in2(B_imme), .in3(U_imme), .in4(J_imme), .out(Immediate), .sel(ImmSel));  // open: in5, in6, in7
  assign I_imme = {{20{Instruction[31]}}, Instruction[31:20]};  // Bit_Extender bit_extender_13
  Shifter #(.width(32)) shifter_8 (.in(bit_extender_1_out), .\dist (5'b01011), .out(shifter_8_out));
  Shifter #(.width(32)) shifter_9 (.in(bit_extender_2_out), .\dist (5'b00001), .out(shifter_9_out));
  Shifter #(.width(32)) shifter_10 (.in(bit_extender_3_out), .\dist (5'b00101), .out(shifter_10_out));
  Shifter #(.width(32)) shifter_11 (.in(bit_extender_4_out), .\dist (5'b01100), .out(shifter_11_out));
  Adder #(.width(32)) adder_1 (.a(shifter_8_out), .b(shifter_9_out), .out(adder_1_out));  // open: cin, cout
  Adder #(.width(32)) adder_2 (.a(shifter_10_out), .b(shifter_11_out), .out(adder_2_out));  // open: cin, cout
  Adder #(.width(32)) adder_3 (.a(shifter_1_out), .b(shifter_2_out), .out(adder_3_out));  // open: cin, cout
  Adder #(.width(32)) adder_4 (.a(shifter_4_out), .b(shifter_5_out), .out(adder_4_out));  // open: cin, cout
  Adder #(.width(32)) adder_5 (.a(shifter_6_out), .b(shifter_7_out), .out(adder_5_out));  // open: cin, cout
  Adder #(.width(32)) adder_6 (.a(adder_1_out), .b(adder_2_out), .out(B_imme));  // open: cin, cout
  Adder #(.width(32)) adder_7 (.a(bit_extender_5_out), .b(adder_3_out), .out(S_imme));  // open: cin, cout
  Adder #(.width(32)) adder_8 (.a(adder_4_out), .b(adder_5_out), .out(J_imme));  // open: cin, cout

  // Notes on the sheet:
  //   INPUTS to your circuit
  //   DON'T CHANGE THE LOCATIONS OF THE INPUTS AND OUTPUTS!
  //   OUTPUT from your circuit
endmodule
